# Fritzing sketch Word ClockILI9641ESP32C3 (saved by Fritzing 0.9.4)
circuit board: 8.41149cm x 6.00197cm

parts:
  R13 = Resistor [tolerance=±5% resistance=22k package=THT]
  USB = USB Connectors [package=usb-microb]  # not connected
  ESP32-C3-12F = Arduino Nano (Rev3.0)
  LDR = Photocell (LDR) [package=THT]
  IL9341_Display = female pin header, 9 pins [form="♀ (female)"]
  Q2 = NPN-Transistor [part_number=2N2222 package="TO92 [THT]"]
  R14 = Resistor [tolerance=±5% resistance=10k package=THT]
  R15 = Resistor [tolerance=±5% resistance=1k package=THT]
  Connector = male pin header, 2 pins [form="♂ (male)"]

nets:
  N1: R13.Pin_0, ESP32-C3-12F.GND, LDR.pin_1, Connector.pin1
  N2: R13.Pin_1, ESP32-C3-12F.D7
  N3: ESP32-C3-12F.D0/RX, R15.Pin_1
  N4: ESP32-C3-12F.D8, LDR.pin_0, Q2.C, R14.Pin_0, Connector.pin2
  N5: ESP32-C3-12F.5V, IL9341_Display.pin3
  N6: ESP32-C3-12F.A7, IL9341_Display.pin4
  N7: ESP32-C3-12F.A5, IL9341_Display.pin7
  N8: ESP32-C3-12F.A3, IL9341_Display.pin5
  N9: ESP32-C3-12F.A2, IL9341_Display.pin6
  N10: ESP32-C3-12F.3V3, IL9341_Display.pin8
  N11: ESP32-C3-12F.D13/SCK, IL9341_Display.pin9
  N12: IL9341_Display.pin2, Q2.E
  N13: Q2.B, R14.Pin_1, R15.Pin_0

notes:
  RX
  TX
  D12
  +
  IO1
  NC
  IO2
  IO3
  IO5
  IO4
  3V3
  IO9
  EN
  IO7
  IO0
  5V
  IO18
  IO19
  ADC
  IO10
  IO6
  GND
  IO8
  SDO/MISO
  LED
  SCK
  SDI/MOSI
  DC/RS
  RESET
  CS
  VCC
